// Logisim project sCPU.circ as structural Verilog: 1 circuit, main circuit main
module main (
);

  wire clock_1_out, clock_2_out, reset;
  wire [7:0] CMD, PC;

  Clock clock_1 (.out(clock_1_out));
  Counter counter_1 (.clr(reset), .clk(clock_1_out), .Q(PC));  // open: load, up, count, D, carry
  Button button_1 (.out(reset));
  // Probe on PC
  Clock clock_2 (.out(clock_2_out));
  RAM ram_1 (.addr(PC), .oe(1'b1), .clk(clock_2_out), .dout(CMD));  // open: we, din
  // Probe on CMD
endmodule
