// Logisim project minirv.circ as structural Verilog: 1 circuit, main circuit main
module main (
);

  wire clock_1_out, clock_2_out, clock_3_out, decoder_1_out0, decoder_1_out1, decoder_1_out2, decoder_1_out3,
       decoder_1_out4, decoder_1_out5, decoder_1_out6, decoder_1_out7, decoder_1_out8, decoder_1_out9,
       decoder_1_out10, decoder_1_out11, decoder_1_out12, decoder_1_out13, decoder_1_out14, decoder_1_out15,
       reset;
  wire [3:0] rd_selector, rs1_selector, rs2_selector;
  wire [6:0] opcode;
  wire [15:0] PC_data;
  wire [31:0] R0_q, R1_q, R2_q, R3_q, R4_q, R5_q, R6_q, R7_q, R8_q, R9_q, R10_q, R11_q, R12_q, R13_q, R14_q,
       R15_q, rs1_data, rs2_data, write_data;
  wire [31:7] RAM_data;

  Counter #(.max('hffff), .width(16)) PC_counter (
    .clr(reset), .clk(clock_1_out), .Q(PC_data));  // open: load, up, count, D, carry
  Clock clock_1 (.out(clock_1_out));
  Clock clock_2 (.out(clock_2_out));
  // NoConnect on decoder_1_out0
  Decoder #(.select(4)) decoder_1 (
    .out0(decoder_1_out0), .out1(decoder_1_out1), .out2(decoder_1_out2), .out3(decoder_1_out3),
    .out4(decoder_1_out4), .out5(decoder_1_out5), .out6(decoder_1_out6), .out7(decoder_1_out7),
    .out8(decoder_1_out8), .out9(decoder_1_out9), .out10(decoder_1_out10), .out11(decoder_1_out11),
    .out12(decoder_1_out12), .out13(decoder_1_out13), .out14(decoder_1_out14), .out15(decoder_1_out15),
    .sel(rd_selector));  // open: en
  Button reset_button (.out(reset));
  Register #(.width(32)) R0 (.D(write_data), .en(1'b0), .clk(clock_2_out), .Q(R0_q), .clr(1'b1));
  Register #(.width(32)) R8 (.D(write_data), .en(decoder_1_out8), .clk(clock_2_out), .Q(R8_q), .clr(reset));
  Register #(.width(32)) R1 (.D(write_data), .en(decoder_1_out1), .clk(clock_2_out), .Q(R1_q), .clr(reset));
  Register #(.width(32)) R9 (.D(write_data), .en(decoder_1_out9), .clk(clock_2_out), .Q(R9_q), .clr(reset));
  Register #(.width(32)) R2 (.D(write_data), .en(decoder_1_out2), .clk(clock_2_out), .Q(R2_q), .clr(reset));
  Register #(.width(32)) R10 (.D(write_data), .en(decoder_1_out10), .clk(clock_2_out), .Q(R10_q), .clr(reset));
  Register #(.width(32)) R3 (.D(write_data), .en(decoder_1_out3), .clk(clock_2_out), .Q(R3_q), .clr(reset));
  Register #(.width(32)) R11 (.D(write_data), .en(decoder_1_out11), .clk(clock_2_out), .Q(R11_q), .clr(reset));
  Register #(.width(32)) R4 (.D(write_data), .en(decoder_1_out4), .clk(clock_2_out), .Q(R4_q), .clr(reset));
  Register #(.width(32)) R12 (.D(write_data), .en(decoder_1_out12), .clk(clock_2_out), .Q(R12_q), .clr(reset));
  RAM #(.addrWidth(16), .asyncread("true"), .byteenables("byteEnables"), .dataWidth(32), .\type ("nonvolatile")) ram_1 (
    .addr(PC_data), .clk(clock_3_out), .dout({RAM_data, opcode}));  // open: we, oe, din, be3, be2, be1, be0
  Clock clock_3 (.out(clock_3_out));
  Register #(.width(32)) R5 (.D(write_data), .en(decoder_1_out5), .clk(clock_2_out), .Q(R5_q), .clr(reset));
  Register #(.width(32)) R13 (.D(write_data), .en(decoder_1_out13), .clk(clock_2_out), .Q(R13_q), .clr(reset));
  Register #(.width(32)) R6 (.D(write_data), .en(decoder_1_out6), .clk(clock_2_out), .Q(R6_q), .clr(reset));
  Register #(.width(32)) R14 (.D(write_data), .en(decoder_1_out14), .clk(clock_2_out), .Q(R14_q), .clr(reset));
  Register #(.width(32)) R7 (.D(write_data), .en(decoder_1_out7), .clk(clock_2_out), .Q(R7_q), .clr(reset));
  Register #(.width(32)) R15 (.D(write_data), .en(decoder_1_out15), .clk(clock_2_out), .Q(R15_q), .clr(reset));
  // Probe on {RAM_data, opcode}
  Multiplexer #(.select(4), .width(32)) multiplexer_1 (
    .in0(R0_q), .in1(R1_q), .in2(R2_q), .in3(R3_q), .in4(R4_q), .in5(R5_q), .in6(R6_q), .in7(R7_q),
    .in8(R8_q), .in9(R9_q), .in10(R10_q), .in11(R11_q), .in12(R12_q), .in13(R13_q), .in14(R14_q),
    .in15(R15_q), .out(rs1_data), .sel(rs1_selector));
  Multiplexer #(.select(4), .width(32)) multiplexer_2 (
    .in0(R0_q), .in1(R1_q), .in2(R2_q), .in3(R3_q), .in4(R4_q), .in5(R5_q), .in6(R6_q), .in7(R7_q),
    .in8(R8_q), .in9(R9_q), .in10(R10_q), .in11(R11_q), .in12(R12_q), .in13(R13_q), .in14(R14_q),
    .in15(R15_q), .out(rs2_data), .sel(rs2_selector));
  Bit_Extender #(.in_width(5), .out_width(4)) bit_extender_1 (.in(RAM_data[11:7]), .out(rd_selector));

  // Other names for the same wires on the sheet: RAM_data[6:0] = opcode
endmodule
